# Fritzing sketch E-vlampios (saved by Fritzing 0.9.3b)
breadboards: 3

parts:
  hc-sr4 = hc-sr04
  Raspberry_Pi_1 = Raspberry Pi 3 [part_number=RPI-3-V1.2]
  hc-sr5 = hc-sr04
  hc-sr6 = hc-sr04
  M1 = DC Motor
  IC1 = L293D [package=THT]
  M2 = DC Motor
  R5 = Resistor [tolerance=±5% resistance=2k package="1206 [SMD]"]
  R6 = Resistor [tolerance=±5% resistance=2k package="1206 [SMD]"]
  R7 = Resistor [tolerance=±5% resistance=2k package="1206 [SMD]"]
  R8 = Resistor [tolerance=±5% resistance=1k package="1206 [SMD]"]
  R9 = Resistor [tolerance=±5% resistance=1k package="1206 [SMD]"]
  R10 = Resistor [tolerance=±5% resistance=1k package="1206 [SMD]"]
  Grove1 = Grove 3 Axis Digital Accelerometer 16g
  hc-sr7 = hc-sr04
  hc-sr8 = hc-sr04
  R12 = Resistor [tolerance=±5% resistance=2k package="1206 [SMD]"]
  R13 = Resistor [tolerance=±5% resistance=1k package="1206 [SMD]"]
  R15 = Resistor [tolerance=±5% resistance=2k package="1206 [SMD]"]
  R16 = Resistor [tolerance=±5% resistance=1k package="1206 [SMD]"]
  R20 = PHOTOCELL [package=photocell]
  C1 = Electrolytic Capacitor [capacitance=1µF voltage=50V package="0807 [SMD, electrolytic]"]
  Part1 = Logic Level Converter
  USBTTL1 = USB A Plug
  USBTTL3 = Micro USB B Plug
  Part2 = Arduino Mega 2560 (Rev3)
  CAMERA1 = TTL Serial JPEG Camera
  USBTTL4 = USB TTL Serial Cable

nets:
  VCC: hc-sr4.VCC, Raspberry_Pi_1.5V, hc-sr5.VCC, hc-sr6.VCC, hc-sr7.VCC, hc-sr8.VCC
  N1: hc-sr4.Trig, Raspberry_Pi_1.GPIO25
  N2: hc-sr4.Echo, R10.Pin_1
  GND: hc-sr4.GND, Raspberry_Pi_1.GND, hc-sr5.GND, hc-sr6.GND, R5.Pin_1, R6.Pin_1, R7.Pin_1, hc-sr8.GND, R15.Pin_1, C1.+
  N3: Raspberry_Pi_1.3v3, Part1.LV
  N4: Raspberry_Pi_1.GPIO2, Part1.TX_LV
  N5: Raspberry_Pi_1.GPIO3, Part1.RX_LV
  N6: Raspberry_Pi_1.GPIO17, R5.Pin_0, R8.Pin_0
  N7: Raspberry_Pi_1.GPIO27, R6.Pin_0, R9.Pin_0
  N8: Raspberry_Pi_1.GPIO22, R7.Pin_0, R10.Pin_0
  N9: Raspberry_Pi_1.GPIO10, hc-sr8.Trig
  N10: Raspberry_Pi_1.GPIO9, hc-sr7.Echo, R12.Pin_0, R16.Pin_0, R16.Pin_1
  N11: Raspberry_Pi_1.GPIO21, R20.P$2, C1.-
  N12: Raspberry_Pi_1.GPIO20, R20.P$1
  N13: Raspberry_Pi_1.GPIO7, hc-sr7.Trig
  N14: Raspberry_Pi_1.GPIO8, hc-sr8.Echo, R13.Pin_0, R13.Pin_1, R15.Pin_0
  N15: Raspberry_Pi_1.GPIO24, hc-sr5.Trig
  N16: Raspberry_Pi_1.GPIO23, hc-sr6.Trig
  N17: hc-sr5.Echo, R9.Pin_1
  N18: hc-sr6.Echo, R8.Pin_1
  N19: M1.pin_1, IC1.Out_1_(_Controlled_by_Enable_1_), Part1.RX_HV
  N20: M1.pin_2, IC1.In_2, Part1.TX_HV
  N21: IC1.0V, Part1.GND
  N22: IC1.+Vmotor, Part1.HV
  N23: IC1.Enable_2, M2.pin_2
  N24: IC1.Out_4_(_Controlled_by_Enable_2_), M2.pin_1
  GND_2: Grove1.GND, Part2.GND
  VCC_2: Grove1.VCC, Part2.3V3
  N25: Grove1.SDA, Part2.D20/SDA
  N26: Grove1.SCL, Part2.D21/SCL
  N27: hc-sr7.GND, R12.Pin_1
  N28: USBTTL1.usb, USBTTL3.RX
  N29: CAMERA1.TX, USBTTL4.TX
  N30: CAMERA1.RX, USBTTL4.RX
  GND_3: CAMERA1.GND, USBTTL4.GND
  5V: CAMERA1.5V, USBTTL4.5V

notes:
  12V

custom parts:
  TTL Serial JPEG Camera: TTL Serial JPEG Camera with NTSC Out
